// Digital circuit 2BitShifter.dig as structural Verilog
module _2BitShifter (
  input  [1:0] A,
  input  Cin,
  output [1:0] R,
  output Cout
);


  assign Cout = A[1];
  assign R = {A[0], Cin};
endmodule
