// Digital circuit 8BitComparer.dig as structural Verilog
module _8BitComparer (
  input  [7:0] A,
  input  [7:0] B,
  output A_gt_B,
  output A_lt_B,
  output A_eq_B
);

  wire _4bitcomparer_1_p4, _4bitcomparer_1_p5, _4bitcomparer_1_p6, _4bitcomparer_2_p5, _4bitcomparer_2_p6;

  // _4BitComparer _4bitcomparer_1: pin names not known; wires that end beside it: A[7:4], B[7:4], 1'b1, _4bitcomparer_1_p4, _4bitcomparer_1_p5, _4bitcomparer_1_p6
  // _4BitComparer _4bitcomparer_2: pin names not known; wires that end beside it: A[3:0], B[3:0], _4bitcomparer_1_p4, A_eq_B, _4bitcomparer_2_p5, _4bitcomparer_2_p6
  or or_1 (A_gt_B, _4bitcomparer_2_p5, _4bitcomparer_1_p5);
  or or_2 (A_lt_B, _4bitcomparer_2_p6, _4bitcomparer_1_p6);
endmodule
