// Digital circuit 8BitMultiplicationPartialStep.dig as structural Verilog
module _8BitMultiplicationPartialStep (
  input  A,
  input  [7:0] B,
  output [7:0] R
);

  // _4BitMultiplicationPartialStep _4bitmultiplicationpartialstep_1: pin names not known; wires that end beside it: A, B[3:0], R[3:0]
  // _4BitMultiplicationPartialStep _4bitmultiplicationpartialstep_2: pin names not known; wires that end beside it: A, B[7:4], R[7:4]
endmodule
