// Digital circuit 8BitMultiplier.dig as structural Verilog
module _8BitMultiplier (
  input  [3:0] A,
  input  [3:0] B,
  output [7:0] R
);

  wire _8bitadder_1_p4, _8bitadder_1_p5, _8bitadder_2_p4, _8bitadder_2_p5, bitshifter_1_p2, bitshifter_2_p2,
       bitshifter_3_p2, bitshifter_4_p2, bitshifter_5_p2, bitshifter_6_p2, bitshifter_7_p2, bitshifter_8_p2;
  wire [3:0] _4bitmultiplier_1_p3, _4bitmultiplier_2_p3, _4bitmultiplier_3_p3, _4bitmultiplier_4_p3;

  // _4BitMultiplier _4bitmultiplier_1: pin names not known; wires that end beside it: A[1:0], B[1:0], _4bitmultiplier_1_p3
  // _4BitMultiplier _4bitmultiplier_2: pin names not known; wires that end beside it: A[1:0], B[3:2], _4bitmultiplier_2_p3
  // _4BitMultiplier _4bitmultiplier_3: pin names not known; wires that end beside it: A[3:2], B[1:0], _4bitmultiplier_3_p3
  // BitShifter bitshifter_1: pin names not known; wires that end beside it: {4'b0000, _4bitmultiplier_2_p3}, bitshifter_1_p2
  // _4BitMultiplier _4bitmultiplier_4: pin names not known; wires that end beside it: A[3:2], B[3:2], _4bitmultiplier_4_p3
  // BitShifter bitshifter_2: pin names not known; wires that end beside it: bitshifter_1_p2, bitshifter_2_p2
  // BitShifter bitshifter_3: pin names not known; wires that end beside it: {4'b0000, _4bitmultiplier_3_p3}, bitshifter_3_p2
  // BitShifter bitshifter_4: pin names not known; wires that end beside it: {4'b0000, _4bitmultiplier_4_p3}, bitshifter_4_p2
  // _8BitAdder _8bitadder_1: pin names not known; wires that end beside it: {4'b0000, _4bitmultiplier_1_p3}, bitshifter_2_p2, 1'b0, _8bitadder_1_p4, _8bitadder_1_p5
  // BitShifter bitshifter_5: pin names not known; wires that end beside it: bitshifter_3_p2, bitshifter_5_p2
  // BitShifter bitshifter_6: pin names not known; wires that end beside it: bitshifter_4_p2, bitshifter_6_p2
  // BitShifter bitshifter_7: pin names not known; wires that end beside it: bitshifter_6_p2, bitshifter_7_p2
  // _8BitAdder _8bitadder_2: pin names not known; wires that end beside it: _8bitadder_1_p4, bitshifter_5_p2, _8bitadder_1_p5, _8bitadder_2_p4, _8bitadder_2_p5
  // BitShifter bitshifter_8: pin names not known; wires that end beside it: bitshifter_7_p2, bitshifter_8_p2
  // _8BitAdder _8bitadder_3: pin names not known; wires that end beside it: _8bitadder_2_p4, bitshifter_8_p2, _8bitadder_2_p5, R
endmodule
