// Digital circuit 8BitSubtractor.dig as structural Verilog
module _8BitSubtractor (
  input  [7:0] A,
  input  [7:0] B,
  output [7:0] Subtract,
  output Cout
);

  wire [7:0] not_1_out;

  assign not_1_out = ~B;  // Not not_1, 8 bits wide
  // _8BitAdder _8bitadder_1: pin names not known; wires that end beside it: A, not_1_out, 1'b1, Subtract, Cout
endmodule
