// Digital circuit Clock2Ticks.dig as structural Verilog
module Clock2Ticks (
  input  _1,
  input  _2,
  input  clk,
  input  clk_2,
  output [7:0] T,
  output out_5,
  output out_6,
  output [3:0] out_8,
  output [3:0] out_9
);

  wire counter_2_ovf, d_ff_1_nq, d_ff_1_q, d_ff_2_q, not_1_out;

  not not_1 (not_1_out, clk_2);
  Counter #(.Bits(4)) counter_1 (.en(clk_2), .C(clk_2), .clr(1'b0), .out(out_8));  // open: ovf
  Register #(.Bits(4)) register_1 (.D(4'b0000), .C(not_1_out), .en(not_1_out), .Q(out_9));
  D_FF d_ff_1 (.D(d_ff_1_nq), .C(_1), .Q(d_ff_1_q), .nQ(d_ff_1_nq));
  not not_2 (out_5, clk);
  D_FF d_ff_2 (.D(d_ff_1_q), .C(_2), .Q(d_ff_2_q));  // open: nQ
  Counter #(.Bits(8)) counter_2 (.en(d_ff_2_q), .C(_1), .clr(counter_2_ovf), .out(T), .ovf(counter_2_ovf));

  assign out_6 = clk;
endmodule
