// Digital circuit DisplayUla.dig as structural Verilog
module DisplayUla (
  input  [7:0] A,
  input  [7:0] B,
  input  [2:0] Op,
  input  C,
  output A_gt_B,
  output A_eq_B,
  output A_lt_B
);

  wire [3:0] register_1_q;
  wire [7:0] ulaopcodes_1_r;
  wire [7:4] register_1_q_2;

  UlaOpcodes ulaopcodes_1 (
    .A(A), .B(B), .Op(Op), .R(ulaopcodes_1_r), .A_gt_B(A_gt_B), .A_lt_B(A_lt_B), .A_eq_B(A_eq_B));
  Register #(.Bits(8)) register_1 (.D(ulaopcodes_1_r), .C(C), .en(1'b1), .Q({register_1_q_2, register_1_q}));
  Seven_Seg_Hex seven_seg_hex_1 (.d(register_1_q_2), .dp(1'b0));
  Seven_Seg_Hex seven_seg_hex_2 (.d(register_1_q), .dp(1'b0));
endmodule
