// Digital circuit FDX.dig as structural Verilog
module FDX (
  input  [7:0] A,
  input  [7:0] B,
  input  [2:0] Op,
  input  clk,
  input  clk_2,
  output [3:0] out_6,
  output [7:0] out_7,
  output [2:0] OP_2,
  output [3:0] Addr
);

  wire isfive3bit_1__5, not_1_out, not_2_out, not_3_out, not_4_out, not_5_out, not_6_out;
  wire [3:0] counter_1_out, ulaopcodes_1_r, ulaopcodes_1_r_2;
  wire [7:0] demultiplexer_2_out_0, demultiplexer_2_out_1, or_1_out, register_1_q, register_3_q,
       ulaopcodes_2_r;
  wire [7:4] register_2_q;
  wire [10:0] demultiplexer_1_out_1;
  wire [10:8] Ram_d;

  not not_1 (not_1_out, clk_2);
  Counter #(.Bits(4)) counter_1 (.en(not_1_out), .C(not_1_out), .clr(1'b0), .out(counter_1_out));  // open: ovf
  not not_2 (not_2_out, not_1_out);
  not not_3 (not_3_out, not_2_out);
  assign or_1_out = demultiplexer_2_out_0 | {ulaopcodes_1_r_2, ulaopcodes_1_r};  // Or or_1, 8 bits wide
  not not_4 (not_4_out, not_1_out);
  Multiplexer #(.Bits(4)) multiplexer_1 (.sel(not_3_out), .in_0(Addr), .in_1(counter_1_out), .out(out_6));
  RAMDualPort #(.AddrBits(4), .Bits(11)) Ram (
    .A(out_6), .Din({11{1'b1}}), .str(1'b0), .C(1'b1), .ld(1'b1), .D({Ram_d, out_7}));
  Register #(.Bits(8)) register_1 (.D(or_1_out), .C(not_4_out), .en(not_4_out), .Q(register_1_q));
  Demultiplexer #(.Bits(11)) demultiplexer_1 (
    .sel(not_5_out), .in({Ram_d, out_7}), .out_1(demultiplexer_1_out_1));  // open: out_0
  not not_5 (not_5_out, not_2_out);
  Register #(.Bits(11)) register_2 (
    .D(demultiplexer_1_out_1), .C(not_2_out), .en(not_2_out), .Q({OP_2, register_2_q, Addr}));
  Demultiplexer #(.Bits(8)) demultiplexer_2 (
    .sel(not_6_out), .in(out_7), .out_0(demultiplexer_2_out_0), .out_1(demultiplexer_2_out_1));
  not not_6 (not_6_out, isfive3bit_1__5);
  Isfive3Bit isfive3bit_1 (.Op(OP_2), ._5(isfive3bit_1__5));
  UlaOpcodes ulaopcodes_1 (
    .A(register_1_q), .B(demultiplexer_2_out_1), .Op(OP_2), .R({ulaopcodes_1_r_2, ulaopcodes_1_r}));  // open: A_gt_B, A_lt_B, A_eq_B
  Seven_Seg_Hex seven_seg_hex_1 (.d(ulaopcodes_1_r_2), .dp(1'b0));
  Seven_Seg_Hex seven_seg_hex_2 (.d(ulaopcodes_1_r), .dp(1'b0));
  UlaOpcodes ulaopcodes_2 (.A(A), .B(B), .Op(Op), .R(ulaopcodes_2_r));  // open: A_gt_B, A_lt_B, A_eq_B
  Register #(.Bits(8)) register_3 (.D(ulaopcodes_2_r), .C(clk), .en(1'b1), .Q(register_3_q));
  Seven_Seg_Hex seven_seg_hex_3 (.d(register_3_q[7:4]), .dp(1'b0));
  Seven_Seg_Hex seven_seg_hex_4 (.d(register_3_q[3:0]), .dp(1'b0));
endmodule
