// Digital circuit Isfive3Bit.dig as structural Verilog
module Isfive3Bit (
  input  [2:0] Op,
  output _5
);

  Decoder #(.Selector_Bits(3)) decoder_1 (
    .sel(Op), .out_5(_5));  // open: out_0, out_1, out_2, out_3, out_4, out_6, out_7
endmodule
