// Digital circuit UlaOpcodes.dig as structural Verilog
module UlaOpcodes (
  input  [7:0] A,
  input  [7:0] B,
  input  [2:0] Op,
  output [7:0] R,
  output A_gt_B,
  output A_lt_B,
  output A_eq_B
);

  wire _8bitcomparer_1_a_eq_b, _8bitcomparer_1_a_gt_b, _8bitcomparer_1_a_lt_b, decoder_1_out_0,
       decoder_1_out_1, decoder_1_out_2, decoder_1_out_3, decoder_1_out_4;
  wire [7:0] _8bitadder_1_p4, _8bitmultiplicationpartialstep_1_r, _8bitmultiplicationpartialstep_2_r,
       _8bitmultiplicationpartialstep_3_r, _8bitmultiplicationpartialstep_4_r, _8bitmultiplier_1_r,
       _8bitsubtractor_1_subtract, bitshifter_1_p2;

  // _8BitAdder _8bitadder_1: pin names not known; wires that end beside it: A, B, 1'b0, _8bitadder_1_p4
  _8BitComparer _8bitcomparer_1 (
    .A(A), .B(B), .A_gt_B(_8bitcomparer_1_a_gt_b), .A_lt_B(_8bitcomparer_1_a_lt_b),
    .A_eq_B(_8bitcomparer_1_a_eq_b));
  _8BitSubtractor _8bitsubtractor_1 (.A(A), .B(B), .Subtract(_8bitsubtractor_1_subtract));  // open: Cout
  // BitShifter bitshifter_1: pin names not known; wires that end beside it: A, bitshifter_1_p2
  _8BitMultiplier _8bitmultiplier_1 (.A(A[3:0]), .B(B[3:0]), .R(_8bitmultiplier_1_r));
  Decoder #(.Selector_Bits(3)) decoder_1 (
    .sel(Op), .out_0(decoder_1_out_0), .out_1(decoder_1_out_1), .out_2(decoder_1_out_2),
    .out_3(decoder_1_out_3), .out_4(decoder_1_out_4));  // open: out_5, out_6, out_7
  _8BitMultiplicationPartialStep _8bitmultiplicationpartialstep_1 (
    .A(decoder_1_out_0), .B(_8bitadder_1_p4), .R(_8bitmultiplicationpartialstep_1_r));
  and and_1 (A_gt_B, _8bitcomparer_1_a_gt_b, decoder_1_out_1);
  and and_2 (A_lt_B, _8bitcomparer_1_a_lt_b, decoder_1_out_1);
  and and_3 (A_eq_B, _8bitcomparer_1_a_eq_b, decoder_1_out_1);
  _8BitMultiplicationPartialStep _8bitmultiplicationpartialstep_2 (
    .A(decoder_1_out_2), .B(_8bitsubtractor_1_subtract), .R(_8bitmultiplicationpartialstep_2_r));
  _8BitMultiplicationPartialStep _8bitmultiplicationpartialstep_3 (
    .A(decoder_1_out_3), .B(bitshifter_1_p2), .R(_8bitmultiplicationpartialstep_3_r));
  _8BitMultiplicationPartialStep _8bitmultiplicationpartialstep_4 (
    .A(decoder_1_out_4), .B(_8bitmultiplier_1_r), .R(_8bitmultiplicationpartialstep_4_r));
  assign R = _8bitmultiplicationpartialstep_1_r | {8{1'b0}} | _8bitmultiplicationpartialstep_2_r | _8bitmultiplicationpartialstep_3_r | _8bitmultiplicationpartialstep_4_r | {8{1'b0}} | {8{1'b0}} | {8{1'b0}};  // Or or_1, 8 bits wide
endmodule
